# Fritzing sketch better_tone_diagram (saved by Fritzing 0.9.3b)
breadboards: 1

parts:
  ARDUINO_UNO = Arduino Uno (Rev3)
  PIEZO_BUZZER = Piezo Speaker
  R1 = Resistor [tolerance=±5% resistance=1k package=THT]
  D2F1 = D2F-FL Omron Snap Action Limit Switch with Level

nets:
  N1: ARDUINO_UNO.D8, PIEZO_BUZZER.pin2
  N2: ARDUINO_UNO.D9_PWM, R1.Pin_0, D2F1.NO
  N3: ARDUINO_UNO.GND, PIEZO_BUZZER.pin1, R1.Pin_1
  N4: ARDUINO_UNO.5V, D2F1.COM

custom parts:
  D2F-FL Omron Snap Action Limit Switch with Level: Snap action switch with stainless steel lever.

// code stored in the sketch: ATMELEXPERIMENT.ino
#include <Arduino.h>

#include <Servo.h>
#include <Wire.h>
#include <FancyDelay.h> //Props to Unchapped on Github for this awesome library
#include <pitches.h>

//Digital and Analog Pins Used on UNO Board
const int switchPin = 3;    //Digital Pin 2 (No PWM)
const int buzzerPin = 8;    //Digital Pin 8 (No PWM)
const int buttonOnePin = 9; //Digital Pin 9 (PWM)

int switchValue = 0;
int buttonOneValue = 0;

//Ints. related to playing sounds via Piezo Buzzer
int noteC2[] = {NOTE_C2};
int noteDurations[] = {4};
int noteAmount = 1;

//Other 

const bool debugMode = true; //Used to relay values of pins only while also testing
const bool testMode = false; //Used to test only active code 

void setup(){
	Serial.begin(115200); //Serial Start
	pinMode(3, INPUT);  //Limit Switch Pin ()
	pinMode(8, OUTPUT); //Buzzer Output Pin (Piezo Sound Sensor)
	pinMode(9, INPUT);  //Button Input Pin (Red Arcade Button)
	
	Serial.print("Button One initialized on pin number ");
	Serial.print(buttonOnePin, DEC); Serial.println(" ");
	Serial.print("Buzzer initialized on pin number ");
	Serial.print(buzzerPin, DEC); Serial.println(" ");
	Serial.print("Limit Switch initialized on pin number ");
	Serial.print(switchPin, DEC); Serial.println(" ");
}

void loop() {	
	while(debugMode == true) {
	buttonOneValue = digitalRead(buttonOnePin);
	switchValue = digitalRead(switchPin);
	
	Serial.print("Button One Value = ");
	Serial.print(buttonOneValue, DEC); Serial.print(" ");
	FancyDelay(50);
	Serial.print("Switch Value = ");
	Serial.print(switchValue, DEC); Serial.print(" ");
	FancyDelay(50);
	Serial.println(" ");
	}
   
	while(testMode == true) { 
	buttonOneValue = digitalRead(buttonOnePin);
	switchValue = digitalRead(switchPin);
   
	if(switchValue == 1) {
		for (int noteAmount = 0; noteAmount < 1; noteAmount++) {  //Allows for self-correcting note playing
			int noteDuration = 1000 / noteDurations[noteAmount];   // to calculate the note duration, take one second divided by the note type.
			//	    int pause = noteDuration * 1.30; // to distinguish the notes, set a minimum time between them. The note's duration + 30% seems to work well:
			tone(8, noteC2[noteAmount], noteDuration); Serial.println("");
			Serial.println("Switch Activated");
			FancyDelay(2000);
			}
		  }  
    }	
}

// code stored in the sketch: pitches_fritzing.h.ino
#define NOTE_B0  31 
#define NOTE_C1  33 
#define NOTE_CS1 35 
#define NOTE_D1  37 
#define NOTE_DS1 39 
#define NOTE_E1  41 
#define NOTE_F1  44 
#define NOTE_FS1 46 
#define NOTE_G1  49 
#define NOTE_GS1 52 
#define NOTE_A1  55 
#define NOTE_AS1 58 
#define NOTE_B1  62 
#define NOTE_C2  65 
#define NOTE_CS2 69 
#define NOTE_D2  73 
#define NOTE_DS2 78 
#define NOTE_E2  82 
#define NOTE_F2  87 
#define NOTE_FS2 93 
#define NOTE_G2  98 
#define NOTE_GS2 104 
#define NOTE_A2  110 
#define NOTE_AS2 117 
#define NOTE_B2  123 
#define NOTE_C3  131 
#define NOTE_CS3 139 
#define NOTE_D3  147 
#define NOTE_DS3 156 
#define NOTE_E3  165 
#define NOTE_F3  175 
#define NOTE_FS3 185 
#define NOTE_G3  196 
#define NOTE_GS3 208 
#define NOTE_A3  220 
#define NOTE_AS3 233 
#define NOTE_B3  247 
#define NOTE_C4  262 
#define NOTE_CS4 277 
#define NOTE_D4  294 
#define NOTE_DS4 311 
#define NOTE_E4  330 
#define NOTE_F4  349 
#define NOTE_FS4 370 
#define NOTE_G4  392 
#define NOTE_GS4 415 
#define NOTE_A4  440 
#define NOTE_AS4 466 
#define NOTE_B4  494 
#define NOTE_C5  523 
#define NOTE_CS5 554 
#define NOTE_D5  587 
#define NOTE_DS5 622 
#define NOTE_E5  659 
#define NOTE_F5  698 
#define NOTE_FS5 740 
#define NOTE_G5  784 
#define NOTE_GS5 831 
#define NOTE_A5  880 
#define NOTE_AS5 932 
#define NOTE_B5  988 
#define NOTE_C6  1047 
#define NOTE_CS6 1109 
#define NOTE_D6  1175 
#define NOTE_DS6 1245 
#define NOTE_E6  1319 
#define NOTE_F6  1397 
#define NOTE_FS6 1480 
#define NOTE_G6  1568 
#define NOTE_GS6 1661 
#define NOTE_A6  1760 
#define NOTE_AS6 1865 
#define NOTE_B6  1976 
#define NOTE_C7  2093 
#define NOTE_CS7 2217 
#define NOTE_D7  2349 
#define NOTE_DS7 2489 
#define NOTE_E7  2637 
#define NOTE_F7  2794 
#define NOTE_FS7 2960 
#define NOTE_G7  3136 
#define NOTE_GS7 3322 
#define NOTE_A7  3520 
#define NOTE_AS7 3729 
#define NOTE_B7  3951 
#define NOTE_C8  4186 
#define NOTE_CS8 4435 
#define NOTE_D8  4699 
#define NOTE_DS8 4978
